# Fritzing sketch ESP32ボード (saved by Fritzing 0.9.3b)
circuit board: 6.88566cm x 5.36311cm
perfboards: 1

parts:
  J1 = female pin header, 18 pins [form="♀ (female)"]
  J2 = female pin header, 18 pins [form="♀ (female)"]
  J3 = female pin header, 5 pins [form="♀ (female)"]
  J4 = female pin header, 5 pins [form="♀ (female)"]
  R1 = Resistor [tolerance=±5% resistance=10k package=THT]
  C1 = Ceramic Capacitor [capacitance=100nF package="100 mil [THT, multilayer]"]  # not connected
  J5 = male pin header, 2 pins [form="♂ (male)"]
  J6 = male pin header, 2 pins [form="♂ (male)"]
  C2 = Electrolytic Capacitor [capacitance=10µF package="100 mil [THT, electrolytic]"]
  C3 = Ceramic Capacitor [capacitance=100nF package="100 mil [THT, multilayer]"]
  S2 = Pushbutton [package=THT]
  J7 = male pin header, 2 pins [form="♂ (male)"]
  J8 = male pin header, 2 pins [form="♂ (male)"]
  J9 = male pin header, 2 pins [form="♂ (male)"]
  J10 = male pin header, 2 pins [form="♂ (male)"]
  R2 = Resistor [tolerance=±5% resistance=100 package=THT]
  LED1 = LED - 3mm [color="Yellow (595nm)" package="3 mm [THT]"]
  J11 = male pin header, 4 pins [form="♂ (male)"]
  J12 = male pin header, 4 pins [form="♂ (male)"]

nets:
  N1: J1.pin1, J1.pin18, J3.pin3, J4.pin1, J4.pin3, J4.pin5, C3.0, LED1.cathode
  N2: J1.pin4, R2.Pin_1
  N3: J1.pin5, J7.pin1
  N4: J1.pin6, J10.pin1
  N5: J1.pin7, J9.pin1
  N6: J1.pin8, J9.pin2
  N7: J1.pin9, J10.pin2
  N8: J1.pin10, J7.pin2
  N9: J1.pin11, J8.pin2
  N10: J1.pin16, S2.leg0
  N11: J1.pin17, J3.pin4, R1.Pin_0, C2.+
  N12: J2.pin5, J8.pin1
  N13: J2.pin7, J12.pin3
  N14: J2.pin9, J12.pin2
  N15: J2.pin10, J12.pin1
  N16: J2.pin15, J11.pin1
  N17: J2.pin16, J11.pin2
  N18: J3.pin2, J5.pin2, J6.pin2
  N19: J5.pin1, J6.pin1
  N20: R2.Pin_0, LED1.anode
  N21: J11.pin3, J11.pin4
