# Fritzing sketch Omega (saved by Fritzing 0.9.3b)
breadboards: 1

parts:
  Arduino_Due = Arduino Due (Rev2b)
  V1 = DC Power [voltage=5V]
  V2 = DC Power [voltage=9V]
  LF1 = Basic Servo
  LM1 = Basic Servo
  LB1 = Basic Servo
  RF1 = Basic Servo
  RM1 = Basic Servo
  RB1 = Basic Servo
  MS3 = Basic Servo
  MS2 = Basic Servo
  MS1 = Basic Servo
  LF2 = Basic Servo  # not connected
  LM2 = Basic Servo  # not connected
  LB2 = Basic Servo  # not connected
  RF2 = Basic Servo  # not connected
  RM2 = Basic Servo  # not connected
  RB2 = Basic Servo  # not connected
  LF3 = Basic Servo  # not connected
  LM3 = Basic Servo  # not connected
  LB3 = Basic Servo  # not connected
  RF3 = Basic Servo  # not connected
  RM3 = Basic Servo  # not connected
  RB3 = Basic Servo  # not connected
  ESP-32 = ESP-WROOM-32 [ESP-32S] Module [part_number=ESP-WROOM-32]  # not connected

nets:
  N1: Arduino_Due.VIN, V2.V+
  N2: Arduino_Due.D8_PWM, LB1.pulse
  N3: Arduino_Due.D11_PWM, LM1.pulse
  N4: Arduino_Due.D12_PWM, LF1.pulse
  GND: Arduino_Due.GND, V1.V-, V2.V-, LF1.gnd, LM1.gnd, LB1.gnd, RF1.gnd, RM1.gnd, RB1.gnd, MS3.gnd, MS2.gnd, MS1.gnd
  N5: Arduino_Due.D2_PWM, MS3.pulse
  N6: Arduino_Due.D3_PWM, MS2.pulse
  N7: Arduino_Due.D4_PWM/SS1, MS1.pulse
  N8: Arduino_Due.D5_PWM, RB1.pulse
  N9: Arduino_Due.D6_PWM, RM1.pulse
  N10: Arduino_Due.D7_PWM, RF1.pulse
  VCC: V1.V+, LF1.vcc, LM1.vcc, LB1.vcc, RF1.vcc, RM1.vcc, RB1.vcc, MS3.vcc, MS2.vcc, MS1.vcc

custom parts:
  ESP-WROOM-32 [ESP-32S] Module: Espressif ESP-WROOM-32 WiFi/Bluetooth LE microcontroller module also known as the Ai-Thinker ESP-32S module with similar formfactor. The ESP32 is a microcontroller chip with WiFi and BLE capabilities. The chip is developed by Espressif and is the successor to the popular ESP8266 WiFi module.
