# Fritzing sketch サーボ接続ボード (saved by Fritzing 0.9.3b)
perfboards: 1

parts:
  MPU9250_MPU-1 = SparkFun IMU Breakout - MPU-9250 [part_number=" SEN-13762"]
  パーツ1 = Arduino Due (Rev2b)
  J1 = Dagu DGServo 9g header (male) [package=THT]
  J2 = Dagu DGServo 9g header (male) [package=THT]
  J3 = Dagu DGServo 9g header (male) [package=THT]
  J4 = Dagu DGServo 9g header (male) [package=THT]
  J5 = Dagu DGServo 9g header (male) [package=THT]
  J6 = Dagu DGServo 9g header (male) [package=THT]
  J7 = male pin header, 2 pins [form="♂ (male)"]
  J8 = Dagu DGServo 9g header (male) [package=THT]
  J9 = Dagu DGServo 9g header (male) [package=THT]
  J10 = male pin header, 2 pins [form="♂ (male)"]
  J11 = Dagu DGServo 9g header (male) [package=THT]
  J12 = Dagu DGServo 9g header (male) [package=THT]
  J13 = male pin header, 2 pins [form="♂ (male)"]
  J14 = female pin header, 10 pins [form="♀ (female)"]
  J15 = Dagu DGServo 9g header (male) [package=THT]
  J16 = Dagu DGServo 9g header (male) [package=THT]
  J17 = male pin header, 2 pins [form="♂ (male)"]
  J18 = Dagu DGServo 9g header (male) [package=THT]
  J19 = Dagu DGServo 9g header (male) [package=THT]
  J20 = male pin header, 2 pins [form="♂ (male)"]
  J21 = Dagu DGServo 9g header (male) [package=THT]
  J22 = Dagu DGServo 9g header (male) [package=THT]
  J23 = male pin header, 2 pins [form="♂ (male)"]
  J24 = Dagu DGServo 9g header (male) [package=THT]
  J25 = Dagu DGServo 9g header (male) [package=THT]
  J26 = male pin header, 2 pins [form="♂ (male)"]
  J27 = male pin header, 2 pins [form="♂ (male)"]
  J28 = male pin header, 2 pins [form="♂ (male)"]
  microSD1 = AE-MICRO-SD-DIP
  J31 = male pin header, 3 pins [form="♂ (male)"]  # not connected
  J32 = male pin header, 3 pins [form="♂ (male)"]  # not connected
  D1 = Rectifier Diode [part_number=1N4001 package="300 mil [THT]"]

nets:
  N1: MPU9250_MPU-1.SCL/SCLK, パーツ1.D21/SCL3
  N2: MPU9250_MPU-1.SDA/SDI, パーツ1.D20/SDA3
  VDD: MPU9250_MPU-1.VDD, パーツ1.IOREF, J14.pin4, microSD1.VDD
  GND: MPU9250_MPU-1.GND, パーツ1.GND, J1.gnd, J2.gnd, J3.gnd, J4.gnd, J5.gnd, J6.gnd, J8.gnd, J9.gnd, J11.gnd, J12.gnd, J14.pin6, J15.gnd, J16.gnd, J18.gnd, J21.gnd, J22.gnd, J24.gnd, J25.gnd, J26.pin1, J27.pin1, microSD1.VSS
  N3: パーツ1.D18/TX1, J28.pin1
  N4: パーツ1.D19/RX1, J28.pin2
  VCC: J1.Vcc, J2.Vcc, J3.Vcc, J4.Vcc, J8.Vcc, J9.Vcc, J11.Vcc, J12.Vcc, J25.Vcc, J26.pin2
  N5: J1.pulse, J7.pin1
  VCC_2: J5.Vcc, J6.Vcc, J15.Vcc, J16.Vcc, J19.Vcc, J21.Vcc, J22.Vcc, J24.Vcc, J27.pin2, D1.anode
  N6: J8.pulse, J10.pin2
  N7: J9.pulse, J10.pin1
  N8: J11.pulse, J13.pin2
  N9: J14.pin2, microSD1.CD_/_DAT3
  N10: J14.pin3, microSD1.CMD
  N11: J14.pin5, microSD1.CLK
  N12: J14.pin7, microSD1.DAT0
  N13: J15.pulse, J17.pin2
  N14: J19.pulse, J20.pin1
  N15: J21.pulse, J23.pin2
  N16: J22.pulse, J23.pin1
