# Fritzing sketch サーボ調整ツール (saved by Fritzing 0.9.3b)
breadboards: 1

parts:
  U1 = Arduino Pro Mini v13
  LCD1 = LCD screen
  C1 = Ceramic Capacitor [capacitance=100nF package="100 mil [THT, multilayer]"]
  C2 = Ceramic Capacitor [capacitance=100nF package="100 mil [THT, multilayer]"]
  VR1 = Trimpot 3362P [package=3362P]
  V1 = DC Power [voltage=5V]
  V2 = DC Power [voltage=5V]

nets:
  N1: U1.VCC, C2.1, V1.V+
  GND: U1.GND, LCD1.VSS, LCD1.R/W, LCD1.LED-, C1.0, C2.0, VR1.CW, V1.V-, V2.V-
  N2: U1.D12/MISO, LCD1.DB7
  N3: U1.D11_PWM/MOSI, LCD1.DB6
  N4: U1.D10_PWM/SS, LCD1.DB5
  N5: U1.D9_PWM, LCD1.DB4
  N6: U1.D8, LCD1.E
  N7: U1.D7, LCD1.RS
  N8: LCD1.VDD, LCD1.LED+, C1.1, VR1.CCW, V2.V+
  N9: LCD1.V0, VR1.WIPER

custom parts:
  Trimpot 3362P: Various small potentiometers for set-and-forget applications
