# Fritzing sketch 電源スイッチ (saved by Fritzing 0.9.3b)
circuit board: 10cm x 6cm
perfboards: 1

parts:
  S1 = Toggle Switch [package=THT]
  J2 = male pin header, 2 pins [form="♂ (male)"]
  S2 = Toggle Switch [package=THT]
  J3 = male pin header, 2 pins [form="♂ (male)"]
  C1 = Electrolytic Capacitor [capacitance=1mF voltage=16V package="200 mil [THT, electrolytic]"]  # not connected
  C2 = Electrolytic Capacitor [capacitance=1mF voltage=16V package="200 mil [THT, electrolytic]"]
  J4 = male pin header, 2 pins [form="♂ (male)"]
  J5 = male pin header, 2 pins [form="♂ (male)"]
  LED1 = LED - 3mm [color="Blue (430nm)" package="3 mm [THT]"]
  R1 = Resistor [tolerance=±5% resistance=150 package=THT]
  LED2 = LED - 3mm [color="Blue (430nm)" package="3 mm [THT]"]
  R2 = Resistor [tolerance=±5% resistance=150 package=THT]

nets:
  N1: S1.L1, C2.+
  N2: S1.COM, J5.pin1
  N3: J2.pin1, S2.L1
  N4: J2.pin2, J4.pin2
  N5: S2.COM, J4.pin1
  N6: J3.pin2, J5.pin2
  N7: LED1.anode, R1.Pin_1
  N8: LED2.anode, R2.Pin_1
