# Fritzing sketch 電源部（簡易版） (saved by Fritzing 0.9.3b)
perfboards: 1

parts:
  C14 = Ceramic Capacitor 3216 [package="3216 [SMD, multilayer]"]  # not connected
  C15 = Ceramic Capacitor 3216 [package="3216 [SMD, multilayer]"]  # not connected
  C16 = Ceramic Capacitor 3216 [package="3216 [SMD, multilayer]"]  # not connected
  D4 = Rectifier Diode [part_number=1N4002 package="300 mil [THT]"]  # not connected
  J25 = female pin header, 5 pins [form="♀ (female)"]  # not connected
  J26 = female pin header, 5 pins [form="♀ (female)"]  # not connected
  J27 = female pin header, 2 pins [form="♀ (female)"]  # not connected
  J28 = female pin header, 10 pins [form="♀ (female)"]  # not connected
  J29 = female pin header, 5 pins [form="♀ (female)"]  # not connected
  J30 = female pin header, 2 pins [form="♀ (female)"]  # not connected
  J31 = female pin header, 5 pins [form="♀ (female)"]

nets:
  N1: J31.pin1, J31.pin5
